# Fritzing sketch Sketch (saved by Fritzing 0.9.2b)
breadboards: 1

parts:
  MBED1 = mbed
  R1 = Resistor [tolerance=±5% resistance=220 package=THT]
  DI1 = 7-Segment LED Display [package=THT]
  R2 = Resistor [tolerance=±5% resistance=220 package=THT]
  R3 = Resistor [tolerance=±5% resistance=220 package=THT]
  R4 = Resistor [tolerance=±5% resistance=220 package=THT]
  R5 = Resistor [tolerance=±5% resistance=220 package=THT]
  R6 = Resistor [tolerance=±5% resistance=220 package=THT]
  R7 = Resistor [tolerance=±5% resistance=220 package=THT]
  S1 = Pushbutton [package="[THT]"]

nets:
  N1: MBED1.GND, S1.Pin_4
  N2: MBED1.pin24, R3.Pin_1
  N3: MBED1.pin25, R2.Pin_0
  N4: MBED1.pin26, R1.Pin_0
  N5: MBED1.pin27, R4.Pin_1
  N6: MBED1.pin28, R5.Pin_1
  N7: MBED1.pin29, R7.Pin_0
  N8: MBED1.pin30, R6.Pin_0
  N9: MBED1.VOUT, DI1.cathodeA
  N10: R1.Pin_1, DI1.cathodeG
  N11: DI1.cathodeE, R6.Pin_1
  N12: DI1.cathodeD, R7.Pin_1
  N13: DI1.cathodeC, R5.Pin_0
  N14: DI1.cathodeDP, R4.Pin_0
  N15: DI1.cathodeB, R3.Pin_0
  N16: DI1.cathodeF, R2.Pin_1
